# Fritzing sketch Driver panel wiring diagram (saved by Fritzing 0.9.3b)

parts:
  Part1 = Arduino Uno (Rev3)
  S1 = Toggle Switch [package=THT]
  S2 = Toggle Switch [package=THT]
  S3 = Pushbutton [package=THT]
  S4 = Pushbutton [package=THT]
  JP1 = Header 6 [package=1x06-smd]
  JP2 = Header 6 [package=1x06-smd]

nets:
  N1: Part1.D2, S4.leg0, JP2.3
  N2: Part1.D3_PWM, S1.COM, JP2.2
  N3: Part1.D4, JP2.1
  N4: Part1.D5_PWM, S2.COM, JP1.3
  N5: Part1.D6_PWM, S3.leg0, JP1.2
  N6: Part1.D7, JP1.1

notes:
  Missle switch
  Red pushbutton - Gyro
  Black pushbutton - Spare
  Mode Selector
